# Fritzing sketch PWM_Light_Controler_v1_3 (saved by Fritzing 0.9.3b)
circuit board: 6.35cm x 9.43945cm

parts:
  R1 = Resistor [tolerance=±5% resistance=10k package=THT]
  R2 = Resistor [tolerance=±5% resistance=150 package=THT]
  U2 = female pin header, 3 pins [form="♀ (female)" part_number=FQP30N06L]
  R3 = Resistor [tolerance=±5% resistance=10k package=THT]
  R4 = Resistor [tolerance=±5% resistance=150 package=THT]
  U3 = female pin header, 3 pins [form="♀ (female)" part_number=FQP30N06L]
  R5 = Resistor [tolerance=±5% resistance=10k package=THT]
  R6 = Resistor [tolerance=±5% resistance=150 package=THT]
  U4 = female pin header, 3 pins [form="♀ (female)" part_number=FQP30N06L]
  R7 = Resistor [tolerance=±5% resistance=10k package=THT]
  R8 = Resistor [tolerance=±5% resistance=150 package=THT]
  U7 = female pin header, 3 pins [form="♀ (female)" part_number=FQP27P06]
  D1 = Schottky Diode [part_number=1N5817 package="300 mil [THT]"]
  D2 = Schottky Diode [part_number=1N5817 package="300 mil [THT]"]
  D3 = Schottky Diode [part_number=1N5817 package="300 mil [THT]"]
  D4 = Schottky Diode [part_number=1N5817 package="300 mil [THT]"]
  D6 = Schottky Diode [part_number=1N5817 package="300 mil [THT]"]
  D5 = Schottky Diode [part_number=1N5817 package="300 mil [THT]"]
  R12 = Resistor [tolerance=±5% resistance=150 package=THT]
  R10 = Resistor [tolerance=±5% resistance=150 package=THT]
  R9 = Resistor [tolerance=±5% resistance=10k package=THT]
  R11 = Resistor [tolerance=±5% resistance=10k package=THT]
  U5 = female pin header, 3 pins [form="♀ (female)" part_number=FQP30N06L]
  MP2315 = female pin header, 4 pins [form="♀ (female)"]
  J15 = male pin header, 13 pins [form="♂ (male)"]
  J17 = male pin header, 13 pins [form="♂ (male)"]
  J18 = male pin header, 13 pins [form="♂ (male)"]
  U1 = female pin header, 3 pins [form="♀ (female)" part_number=FQP30N06L]
  J20 = female pin header, 2 pins [form="♀ (female)"]
  J19 = female pin header, 2 pins [form="♀ (female)"]
  D7 = Rectifier Diode [part_number=1N4001 package="300 mil [THT]"]
  Q1 = NPN-Transistor [package="TO92 [THT]"]
  R13 = Resistor [tolerance=±5% resistance=220 package=THT]
  C1 = Electrolytic Capacitor [capacitance=1µF package="100 mil [THT, electrolytic]"]
  I2C = male pin header, 5 pins [form="♂ (male)"]
  U6 = rounded female pin header, 3 pins [form="♀ (female rounded)" part_number=FQP30N06L]
  Pir = male pin header, 3 pins [form="♂ (male)"]
  DS1 = DS18B20 1-Wire Temperature Sensor [part_number=DS18B20]
  R14 = Resistor [tolerance=±5% resistance=4.7k package=THT]
  Relæ = male pin header, 3 pins [form="♂ (male)"]
  R15 = Resistor [tolerance=±5% resistance=4.7k package=THT]
  R16 = Resistor [tolerance=±5% resistance=4.7k package=THT]
  ESP32 = DOIT Esp32 DevKit v1 (30 pins long, 11 pins width) [part_number=ESP32S-PIN30]
  MP1584EN-in = female pin header, 2 pins [form="♀ (female)"]
  J32 = female pin header, 2 pins [form="♀ (female)"]
  J33 = female pin header, 2 pins [form="♀ (female)"]
  MP1584EN-out = female pin header, 2 pins [form="♀ (female)"]
  Display = female pin header, 4 pins [form="♀ (female)"]
  DD2712SA = female pin header, 6 pins [form="♀ (female)"]
  J34 = female pin header, 2 pins [form="♀ (female)"]
  C2 = Electrolytic Capacitor [capacitance=1µF package="100 mil [THT, electrolytic]"]
  C3 = Electrolytic Capacitor [capacitance=10µF package="100 mil [THT, electrolytic]"]
  LM2937-3_3 = Voltage Regulator [part_number=LM2937-3,3 package=to220-igo]
  AMS1117 = female pin header, 1 pin [form="♀ (female)"]
  J41 = female pin header, 15 pins [form="♀ (female)"]
  J1 = male pin header, 2 pins [form="♂ (male)" part_number=5512/2]
  J2 = male pin header, 2 pins [form="♂ (male)" part_number=5512/2]
  J3 = male pin header, 2 pins [form="♂ (male)" part_number=5512/2]
  J4 = male pin header, 2 pins [form="♂ (male)" part_number=5512/2]
  J6 = male pin header, 2 pins [form="♂ (male)" part_number=5512/2]
  J7 = male pin header, 3 pins [form="♂ (male)" part_number=5556.02)]
  J42 = female pin header, 2 pins [form="♀ (female)"]
  Relæ_2 = IC, DIP package, 16 pins [chip_label=IC part_number=5722-05]
  J5 = male pin header, 2 pins [form="♂ (male)" part_number=5512/2]
  J43 = female pin header, 36 pins [form="♀ (female)"]  # not connected
  J44 = female pin header, 24 pins [form="♀ (female)"]  # not connected
  J45 = female pin header, 36 pins [form="♀ (female)"]  # not connected
  J46 = female pin header, 24 pins [form="♀ (female)"]  # not connected

nets:
  GND: R1.Pin_0, U2.pin3, R3.Pin_0, U3.pin3, R5.Pin_0, U4.pin3, R7.Pin_0, U7.pin1, R9.Pin_0, R11.Pin_0, U5.pin3, MP2315.pin2, U1.pin3, J19.pin1, J19.pin2, Q1.E, C1.-, I2C.pin3, U6.pin3, Pir.pin3, DS1.GND, ESP32.GND, J32.pin1, J32.pin2, J33.pin1, J33.pin2, Display.pin4, DD2712SA.pin3, DD2712SA.pin4, C2.-, C3.-, LM2937-3_3.GND, J41.pin2, J7.pin1, J42.pin2
  N1: R1.Pin_1, R2.Pin_1, U1.pin1
  N2: R2.Pin_0, J17.pin1, J18.pin1, ESP32.D13
  N3: U2.pin1, R3.Pin_1, R4.Pin_1
  N4: U2.pin2, D2.anode, J2.pin1
  N5: R4.Pin_0, J17.pin2, J18.pin2, ESP32.D12
  N6: U3.pin1, R5.Pin_1, R6.Pin_1
  N7: U3.pin2, D3.anode, J3.pin1
  N8: R6.Pin_0, J17.pin3, J18.pin3, ESP32.D14
  N9: U4.pin1, R7.Pin_1, R8.Pin_1
  N10: U4.pin2, D4.anode, J4.pin1
  N11: R8.Pin_0, J17.pin4, J18.pin4, ESP32.D27
  N12: U7.pin2, J7.pin2, J7.pin3
  24V: U7.pin3, D1.cathode, D2.cathode, D3.cathode, D4.cathode, D6.cathode, D5.cathode, MP2315.pin3, MP1584EN-in.pin1, MP1584EN-in.pin2, DD2712SA.pin5, DD2712SA.pin6, J1.pin2, J2.pin2, J3.pin2, J4.pin2, J6.pin2, J5.pin2
  N13: D1.anode, U1.pin2, J1.pin1
  N14: D6.anode, U6.pin2, J6.pin1
  N15: D5.anode, U5.pin2, J5.pin1
  N16: R12.Pin_0, J17.pin6, J18.pin6, ESP32.D25
  N17: R12.Pin_1, R11.Pin_1, U6.pin1
  N18: R10.Pin_0, J17.pin5, J18.pin5, ESP32.D26
  N19: R10.Pin_1, R9.Pin_1, U5.pin1
  5V: MP2315.pin1, J20.pin1, J20.pin2, D7.cathode, C1.+, I2C.pin5, Pir.pin1, ESP32.VIN, MP1584EN-out.pin1, MP1584EN-out.pin2, DD2712SA.pin1, DD2712SA.pin2, C3.+, LM2937-3_3.IN, AMS1117.pin1, Relæ_2.pin1
  N20: J15.pin1, ESP32.D15, J41.pin3
  N21: J15.pin2, ESP32.D2, J41.pin4
  N22: J15.pin3, ESP32.D4, J41.pin5
  N23: J15.pin4, ESP32.RX2, J41.pin6
  N24: J15.pin5, ESP32.TX2, J41.pin7
  N25: J15.pin6, ESP32.D5, J41.pin8
  N26: J15.pin7, ESP32.D18, J41.pin9
  N27: J15.pin8, ESP32.D19, J41.pin10
  N28: J15.pin9, I2C.pin2, R15.Pin_0, ESP32.D21, Display.pin1, J41.pin11
  N29: J15.pin10, ESP32.RX0, J41.pin12
  N30: J15.pin11, ESP32.TX0, J41.pin13
  N31: J15.pin12, I2C.pin1, R16.Pin_0, ESP32.D22, Display.pin2, J41.pin14
  N32: J15.pin13, ESP32.D23, J41.pin15
  N33: J17.pin7, J18.pin7, Pir.pin2, ESP32.D33
  N34: J17.pin8, J18.pin8, R13.Pin_0, ESP32.D32
  N35: J17.pin9, J18.pin9, DS1.DQ, R14.Pin_1, ESP32.D35
  N36: J17.pin10, J18.pin10, ESP32.D34
  N37: J17.pin11, J18.pin11, ESP32.VN
  N38: J17.pin12, J18.pin12, ESP32.VP
  N39: J17.pin13, J18.pin13, ESP32.EN
  N40: D7.anode, Q1.C, Relæ_2.pin16
  N41: Q1.B, R13.Pin_1
  3.3V: I2C.pin4, DS1.VDD, R14.Pin_0, R15.Pin_1, R16.Pin_1, ESP32.3V3, Display.pin3, J34.pin1, J34.pin2, C2.+, LM2937-3_3.OUT, J41.pin1, J42.pin1
  N42: Relæ.pin1, Relæ_2.pin4, Relæ_2.pin13
  N43: Relæ.pin2, Relæ_2.pin6, Relæ_2.pin11
  N44: Relæ.pin3, Relæ_2.pin8, Relæ_2.pin9

notes:
  PWM Light Controler V1.3
  S.E.K.T. 20210503
  +Power-
  +3.3V
  +5V
  SCL
  SDA
  GND
  NC
  NO
  Power 12/24V

custom parts:
  DOIT Esp32 DevKit v1 (30 pins long, 11 pins width): The DOIT Esp32 DevKit v1 is one of the development board created by DOIT to evaluate the ESP-WROOM-32 module. It is based on the ESP32 microcontroller that boasts Wifi, Bluetooth, Ethernet and Low Power support all in a single chip. (vanepp) made breadboard work, adjusted pin numbering and labels and reduced size of schematic and cleaned up pcb. This chip is 30pins long (2 x15) and 11 pins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
