# Fritzing sketch PWM_Light_Controler_v2_0 (saved by Fritzing 0.9.3b)
circuit board: 6.2cm x 8.9cm
breadboards: 1

parts:
  Q1 = Basic FET N-Channel [part_number=FQP30N06L package="TO220 [THT]"]
  D1 = Schottky Diode [part_number=1N5817 package="300 mil [THT]"]
  J1 = Screw terminal - 2 pins [package=THT]
  ESP32 = DOIT Esp32 DevKit v1 (30 pins long, 11 pins width) [part_number=ESP32S-PIN30]
  12/24V = Power plug
  D2 = Schottky Diode [part_number=1N5817 package="300 mil [THT]"]
  J2 = Screw terminal - 2 pins [package=THT]
  Q3 = Basic FET N-Channel [part_number=FQP30N06L package="TO220 [THT]"]
  D3 = Schottky Diode [part_number=1N5817 package="300 mil [THT]"]
  J3 = Screw terminal - 2 pins [package=THT]
  Q4 = Basic FET N-Channel [part_number=FQP30N06L package="TO220 [THT]"]
  D4 = Schottky Diode [part_number=1N5817 package="300 mil [THT]"]
  J4 = Screw terminal - 2 pins [package=THT]
  Q5 = Basic FET N-Channel [part_number=FQP30N06L package="TO220 [THT]"]
  D5 = Schottky Diode [part_number=1N5817 package="300 mil [THT]"]
  J5 = Screw terminal - 2 pins [package=THT]
  Q6 = Basic FET N-Channel [part_number=FQP30N06L package="TO220 [THT]"]
  D6 = Schottky Diode [part_number=1N5817 package="300 mil [THT]"]
  J6 = Screw terminal - 2 pins [package=THT]
  Relæ = IC, DIP package, 16 pins [chip_label=IC]
  R13 = Resistor [tolerance=±5% resistance=220 package=THT]
  Q2 = Basic FET N-Channel [part_number=FQP30N06L package="TO220 [THT]"]
  Q100 = Basic FET P-Channel [part_number=FQP27P06 package="TO220 [THT]"]
  R1 = Resistor [tolerance=±5% resistance=150 package=THT]
  R2 = Resistor [tolerance=±5% resistance=10k package=THT]
  R3 = Resistor [tolerance=±5% resistance=150 package=THT]
  R4 = Resistor [tolerance=±5% resistance=10k package=THT]
  R6 = Resistor [tolerance=±5% resistance=10k package=THT]
  R5 = Resistor [tolerance=±5% resistance=150 package=THT]
  R8 = Resistor [tolerance=±5% resistance=10k package=THT]
  R7 = Resistor [tolerance=±5% resistance=150 package=THT]
  R9 = Resistor [tolerance=±5% resistance=150 package=THT]
  R10 = Resistor [tolerance=±5% resistance=10k package=THT]
  R12 = Resistor [tolerance=±5% resistance=10k package=THT]
  R11 = Resistor [tolerance=±5% resistance=150 package=THT]
  BME280 = female pin header, 4 pins [form="♀ (female)"]
  Reg_3_3V = female pin header, 3 pins [form="♀ (female)" part_number=Ams1117-3.3]
  MP1584-Out = female pin header, 2 pins [form="♀ (female)"]
  J15 = female pin header, 2 pins [form="♀ (female)"]
  MP1584-IN = female pin header, 2 pins [form="♀ (female)"]
  J17 = female pin header, 2 pins [form="♀ (female)"]
  Q8 = NPN-Transistor [package="TO92 [THT]"]
  D7 = Schottky Diode [part_number=1N5817 package="300 mil [THT]"]
  DS1 = DS18B20 1-Wire Temperature Sensor [part_number=DS18B20]
  R14 = Resistor [tolerance=±5% resistance=4.7k package=THT]
  R15 = Resistor [tolerance=±5% resistance=4.7k package=THT]
  R16 = Resistor [tolerance=±5% resistance=4.7k package=THT]
  Rel2 = male pin header, 3 pins [form="♂ (male)"]
  Rel1 = male pin header, 3 pins [form="♂ (male)"]
  Pir = male pin header, 3 pins [form="♂ (male)"]
  I2C = male pin header, 4 pins [form="♂ (male)"]
  J11 = male pin header, 15 pins [form="♂ (male)"]
  J4_2 = male pin header, 15 pins [form="♂ (male)"]
  J13 = male pin header, 15 pins [form="♂ (male)"]
  J12 = male pin header, 15 pins [form="♂ (male)"]
  1Wire = male pin header, 3 pins [form="♂ (male)"]
  J19 = male pin header, 2 pins [form="♂ (male)"]
  J20 = Screw terminal - 2 pins [package=THT]
  HW-613 = female pin header, 4 pins [form="♀ (female)"]

nets:
  N1: Q1.gate, R1.Pin_1, R2.Pin_0
  N2: Q1.drain, D1.anode, J1.pin2
  GND: Q1.source, ESP32.GND, 12/24V.GND, Q3.source, Q4.source, Q5.source, Q6.source, Q2.source, Q100.gate, R2.Pin_1, R4.Pin_1, R6.Pin_1, R8.Pin_1, R10.Pin_1, R12.Pin_1, BME280.pin2, Reg_3_3V.pin1, J15.pin1, J15.pin2, J17.pin1, J17.pin2, Q8.E, DS1.GND, Pir.pin3, I2C.pin2, J11.pin2, J4_2.pin2, J13.pin2, J12.pin2, 1Wire.pin3, J20.pin2, HW-613.pin3
  24V: D1.cathode, J1.pin1, D2.cathode, J2.pin1, D3.cathode, J3.pin1, D4.cathode, J4.pin1, D5.cathode, J5.pin1, D6.cathode, J6.pin1, Q100.source, MP1584-IN.pin1, MP1584-IN.pin2, HW-613.pin2
  N3: ESP32.3V3, J11.pin1, J12.pin1, J19.pin2
  N4: ESP32.D15, J11.pin3, J12.pin3
  N5: ESP32.D2, J11.pin4, J12.pin4
  N6: ESP32.D4, J11.pin5, J12.pin5
  N7: ESP32.RX2, J11.pin6, J12.pin6
  N8: ESP32.TX2, J11.pin7, J12.pin7
  N9: ESP32.D5, J11.pin8, J12.pin8
  N10: ESP32.D18, J11.pin9, J12.pin9
  N11: ESP32.D19, J11.pin10, J12.pin10
  N12: ESP32.D21, BME280.pin4, R15.Pin_1, I2C.pin4, J11.pin11, J12.pin11
  N13: ESP32.RX0, J11.pin12, J12.pin12
  N14: ESP32.TX0, J11.pin13, J12.pin13
  N15: ESP32.D22, BME280.pin3, R16.Pin_1, I2C.pin3, J11.pin14, J12.pin14
  N16: ESP32.D23, J11.pin15, J12.pin15
  N17: ESP32.EN, J4_2.pin15, J13.pin15
  N18: ESP32.VP, J4_2.pin14, J13.pin14
  N19: ESP32.VN, J4_2.pin13, J13.pin13
  N20: ESP32.D34, J4_2.pin12, J13.pin12
  N21: ESP32.D35, DS1.DQ, R14.Pin_0, J4_2.pin11, J13.pin11, 1Wire.pin2
  N22: ESP32.D32, R13.Pin_0, J4_2.pin10, J13.pin10
  N23: ESP32.D33, Pir.pin2, J4_2.pin9, J13.pin9
  N24: ESP32.D25, R11.Pin_0, J4_2.pin8, J13.pin8
  N25: ESP32.D26, R9.Pin_0, J4_2.pin7, J13.pin7
  N26: ESP32.D27, R7.Pin_0, J4_2.pin6, J13.pin6
  N27: ESP32.D14, R5.Pin_0, J4_2.pin5, J13.pin5
  N28: ESP32.D12, R3.Pin_0, J4_2.pin4, J13.pin4
  N29: ESP32.D13, R1.Pin_0, J4_2.pin3, J13.pin3
  5V: ESP32.VIN, Relæ.pin1, Reg_3_3V.pin3, MP1584-Out.pin1, MP1584-Out.pin2, D7.cathode, Pir.pin1, J4_2.pin1, J13.pin1, HW-613.pin4
  N30: 12/24V.VCC, Q100.drain, J20.pin1
  N31: D2.anode, J2.pin2, Q2.drain
  N32: Q3.gate, R6.Pin_0, R5.Pin_1
  N33: Q3.drain, D3.anode, J3.pin2
  N34: Q4.gate, R8.Pin_0, R7.Pin_1
  N35: Q4.drain, D4.anode, J4.pin2
  N36: Q5.gate, R9.Pin_1, R10.Pin_0
  N37: Q5.drain, D5.anode, J5.pin2
  N38: Q6.gate, R12.Pin_0, R11.Pin_1
  N39: Q6.drain, D6.anode, J6.pin2
  N40: Relæ.pin4, Rel1.pin1
  N41: Relæ.pin6, Rel1.pin2
  N42: Relæ.pin8, Rel1.pin3
  N43: Relæ.pin9, Rel2.pin3
  N44: Relæ.pin11, Rel2.pin2
  N45: Relæ.pin13, Rel2.pin1
  N46: Relæ.pin16, Q8.C, D7.anode
  N47: R13.Pin_1, Q8.B
  N48: Q2.gate, R3.Pin_1, R4.Pin_0
  3.3V: BME280.pin1, Reg_3_3V.pin2, DS1.VDD, R14.Pin_1, R15.Pin_0, R16.Pin_0, I2C.pin1, 1Wire.pin1, J19.pin1

notes:
  Vin
  3V3
  GND
  5V
  PWM Light Controller
  Ver.: 2.0 20210526-1507
  +
  -

custom parts:
  DOIT Esp32 DevKit v1 (30 pins long, 11 pins width): The DOIT Esp32 DevKit v1 is one of the development board created by DOIT to evaluate the ESP-WROOM-32 module. It is based on the ESP32 microcontroller that boasts Wifi, Bluetooth, Ethernet and Low Power support all in a single chip. (vanepp) made breadboard work, adjusted pin numbering and labels and reduced size of schematic and cleaned up pcb. This chip is 30pins long (2 x15) and 11 pins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
